// Logisim project POS_Simplification.circ as structural Verilog: 1 circuit, main circuit main
module main (
  input  x,
  input  y,
  input  z,
  input  e0
);

  wire a0_out, a_out, and_1_out, b_out, c0_out, c_out, d0_out, d_out, e_out, f0_out, f_out, g0_out, g_out,
       not_1_out, not_2_out, not_3_out, or_1_out, or_2_out, or_3_out, or_4_out, or_5_out, or_6_out, or_7_out,
       or_8_out, or_9_out, or_10_out, or_11_out, or_12_out, or_13_out;

  not not_1 (not_1_out, x);
  not not_2 (not_2_out, z);
  not not_3 (not_3_out, y);
  or or_1 (or_1_out, not_1_out, not_2_out);
  or or_2 (or_2_out, not_3_out, not_2_out);
  or or_3 (or_3_out, not_1_out, y);
  or or_4 (or_4_out, x, y);
  or or_5 (or_5_out, x, not_2_out);
  or or_6 (or_6_out, not_3_out, z);
  or or_7 (or_7_out, x, y, not_2_out);
  or or_8 (or_8_out, not_1_out, z);
  or or_9 (or_9_out, x, not_3_out, z);
  or or_10 (or_10_out, x, y, not_2_out);
  or or_11 (or_11_out, not_1_out, y, z);
  or or_12 (or_12_out, not_1_out, not_3_out);
  and and_1 (and_1_out, or_8_out, or_5_out);
  or or_13 (or_13_out, y, z);
  or a (a_out, x, y, z);
  and b (b_out, or_1_out, or_2_out);
  and c (c_out, or_2_out, or_3_out);
  and d (d_out, or_4_out, or_5_out);
  and e (e_out, or_4_out, or_6_out);
  and f (f_out, or_7_out, or_8_out);
  or g (g_out, y, not_2_out);
  and a0 (a0_out, and_1_out, or_13_out);
  and c0 (c0_out, or_1_out, or_9_out);
  and d0 (d0_out, or_9_out, or_10_out, or_11_out);
  and f0 (f0_out, a_out, or_12_out);
  and g0 (g0_out, a_out, or_2_out);
  _7_Segment_Display u_7_segment_display_1 (
    .g(g_out), .f(f_out), .a(a_out), .b(b_out), .e(e_out), .d(d_out), .c(c_out));  // open: dp
  _7_Segment_Display u_7_segment_display_2 (
    .g(g0_out), .f(f0_out), .a(a0_out), .b(or_3_out), .e(e0), .d(d0_out), .c(c0_out));  // open: dp
endmodule
