// Logisim project SOP_Generalized.circ as structural Verilog: 1 circuit, main circuit main
module main (
  input  x,
  input  y,
  input  z
);

  wire a_out, a_prime_out, b_out, b_prime_out, c_out, c_prime_out, d_out, d_prime_out, e_out, e_prime_out,
       f_out, f_prime_out, g_out, g_prime_out, not_1_out, not_2_out, not_3_out, or_1_out, or_2_out, or_3_out,
       or_4_out, or_5_out, or_6_out, x_prime_y_prime_z_out, x_prime_y_prime_z_prime_out, x_prime_yz_out,
       x_prime_yz_prime_out, xy_prime_z_out, xy_prime_z_prime_out, xyz_prime_out;

  not not_1 (not_1_out, x);
  not not_2 (not_2_out, z);
  not not_3 (not_3_out, y);
  and x_prime_y_prime_z (x_prime_y_prime_z_out, not_1_out, not_3_out, z);
  and x_prime_yz_prime (x_prime_yz_prime_out, not_1_out, y, not_2_out);
  and x_prime_yz (x_prime_yz_out, not_1_out, y, z);
  and xy_prime_z_prime (xy_prime_z_prime_out, x, not_3_out, not_2_out);
  and xy_prime_z (xy_prime_z_out, x, not_3_out, z);
  and xyz_prime (xyz_prime_out, x, y, not_2_out);
  and x_prime_y_prime_z_prime (x_prime_y_prime_z_prime_out, not_1_out, not_3_out, not_2_out);
  or or_1 (or_1_out, x_prime_y_prime_z_prime_out, xy_prime_z_out, x_prime_yz_out);
  or or_2 (or_2_out, x_prime_y_prime_z_out, x_prime_yz_prime_out, x_prime_yz_out);
  or or_3 (or_3_out, xy_prime_z_prime_out, xy_prime_z_out, xyz_prime_out);
  or or_4 (or_4_out, x_prime_y_prime_z_prime_out, x_prime_y_prime_z_out, x_prime_yz_prime_out);
  or or_5 (or_5_out, x_prime_y_prime_z_prime_out, x_prime_yz_prime_out, x_prime_yz_out);
  or or_6 (or_6_out, xyz_prime_out, xy_prime_z_prime_out, x_prime_y_prime_z_prime_out);
  or a (a_out, or_2_out, or_3_out);
  or b (b_out, or_4_out, xy_prime_z_prime_out, xyz_prime_out);
  or c (c_out, or_4_out, xyz_prime_out);
  or d (d_out, or_3_out, x_prime_yz_prime_out);
  or e (e_out, xy_prime_z_out, xy_prime_z_prime_out, x_prime_yz_out);
  or f (f_out, or_5_out, xy_prime_z_out);
  or g (g_out, or_5_out, xy_prime_z_prime_out, xyz_prime_out);
  or a_prime (a_prime_out, xy_prime_z_out, x_prime_yz_prime_out);
  or b_prime (b_prime_out, or_4_out, x_prime_yz_out, xyz_prime_out);
  or c_prime (c_prime_out, or_6_out, x_prime_yz_out, x_prime_y_prime_z_out);
  or d_prime (d_prime_out, or_1_out, xyz_prime_out);
  or e_prime (e_prime_out, or_3_out, or_2_out, x_prime_y_prime_z_prime_out);
  or f_prime (f_prime_out, or_2_out, xy_prime_z_out, xy_prime_z_prime_out);
  or g_prime (g_prime_out, or_3_out, x_prime_y_prime_z_out, x_prime_yz_prime_out);
  _7_Segment_Display u_7_segment_display_1 (
    .g(g_out), .f(f_out), .a(a_out), .b(b_out), .e(e_out), .d(d_out), .c(c_out));  // open: dp
  _7_Segment_Display u_7_segment_display_2 (
    .g(g_prime_out), .f(f_prime_out), .a(a_prime_out), .b(b_prime_out), .e(d_prime_out), .d(e_prime_out),
    .c(c_prime_out));  // open: dp

  // Notes on the sheet:
  //   x
  //   y'
  //   z'
  //   x'y'z' +x'yz + xy'z
  //   x'y'z + x'yz' + x'yz
  //   xy'z' + xy'z + xyz'
  //   x'y'z' + x'y'z + x'yz'
  //   x'y'z' + x'yz' + x'yz
  //   x'y'z' + xyz' + xy'z'
endmodule
