// Logisim project sequential_circuit_JK.circ as structural Verilog: 1 circuit, main circuit main
module main (
  input  e0
);

  wire a0_out, a_out, b_out, c0_out, c_out, clock_1_out, D0_out, D1_out, D2_out, D3_out, D4_out, d_out,
       e_out, f0_out, f_out, g0_out, g_out, j_k_ff_1_q, j_k_ff_1_qn, j_k_ff_2_q, j_k_ff_2_qn, j_k_ff_3_q,
       j_k_ff_3_qn, nand_1_out, nand_2_out, nand_3_out, nand_4_out, nand_5_out, nand_6_out, nand_7_out,
       nand_8_out, nand_9_out, nand_10_out, nand_11_out, nand_12_out, nand_13_out, nand_14_out, nand_15_out,
       nand_16_out, nand_17_out, nand_18_out, nand_19_out;

  nand nand_1 (nand_1_out, j_k_ff_2_q, j_k_ff_3_q);
  Clock clock_1 (.out(clock_1_out));
  nand nand_2 (nand_2_out, nand_1_out, nand_1_out);
  nand nand_3 (nand_3_out, j_k_ff_1_qn, j_k_ff_3_qn);
  nand nand_4 (nand_4_out, j_k_ff_1_q, j_k_ff_2_q);
  J_K_Flip_Flop j_k_ff_1 (
    .J(nand_2_out), .clk(clock_1_out), .K(j_k_ff_2_q), .Q(j_k_ff_1_q), .Qn(j_k_ff_1_qn));  // open: preset, en, reset
  J_K_Flip_Flop j_k_ff_2 (
    .J(j_k_ff_3_q), .clk(clock_1_out), .K(nand_3_out), .Q(j_k_ff_2_q), .Qn(j_k_ff_2_qn));  // open: preset, en, reset
  J_K_Flip_Flop j_k_ff_3 (
    .J(nand_4_out), .clk(clock_1_out), .K(1'b1), .Q(j_k_ff_3_q), .Qn(j_k_ff_3_qn));  // open: preset, en, reset
  nand nand_5 (nand_5_out, j_k_ff_1_q, j_k_ff_1_q);
  nand nand_6 (nand_6_out, j_k_ff_3_q, j_k_ff_3_q);
  nand nand_7 (nand_7_out, j_k_ff_2_q, j_k_ff_2_q);
  nand nand_8 (nand_8_out, nand_5_out, nand_7_out);
  nand nand_9 (nand_9_out, j_k_ff_2_q, nand_6_out);
  nand nand_10 (nand_10_out, j_k_ff_1_q, nand_7_out);
  nand nand_11 (nand_11_out, j_k_ff_2_q, j_k_ff_3_q);
  nand nand_12 (nand_12_out, nand_5_out, j_k_ff_2_q);
  nand nand_13 (nand_13_out, nand_5_out, nand_6_out);
  nand nand_14 (nand_14_out, j_k_ff_1_q, j_k_ff_3_q);
  nand nand_15 (nand_15_out, nand_5_out, j_k_ff_2_q, nand_6_out);
  nand nand_16 (nand_16_out, nand_5_out, j_k_ff_3_q);
  nand nand_17 (nand_17_out, nand_7_out, nand_6_out);
  nand nand_18 (nand_18_out, j_k_ff_1_q, nand_6_out);
  nand nand_19 (nand_19_out, j_k_ff_1_q, j_k_ff_2_q);
  nand a (a_out, nand_5_out, nand_7_out, nand_6_out);
  nand b (b_out, nand_8_out, j_k_ff_3_q);
  nand c (c_out, nand_8_out, nand_9_out);
  nand d (d_out, nand_9_out, nand_5_out);
  nand e (e_out, nand_10_out, nand_11_out);
  nand f (f_out, nand_12_out, nand_13_out, nand_14_out);
  nand g (g_out, nand_7_out, j_k_ff_3_q);
  _7_Segment_Display u_7_segment_display_1 (
    .g(g_out), .f(f_out), .a(a_out), .b(b_out), .e(e_out), .d(d_out), .c(c_out));  // open: dp
  nand a0 (a0_out, nand_15_out, nand_14_out);
  nand c0 (c0_out, nand_16_out, nand_17_out, nand_18_out);
  nand D1 (D1_out, a_out, nand_19_out);
  nand f0 (f0_out, nand_12_out, nand_10_out, nand_6_out);
  nand g0 (g0_out, g_out, nand_9_out, nand_5_out);
  _7_Segment_Display u_7_segment_display_2 (
    .g(g0_out), .f(f0_out), .a(a0_out), .b(nand_10_out), .e(e0), .d(D0_out), .c(c0_out));  // open: dp
  nand D2 (D2_out, nand_14_out, nand_11_out);
  nand D4 (D4_out, D2_out, D2_out);
  nand D3 (D3_out, D1_out, D1_out);
  nand D0 (D0_out, D4_out, D3_out);

  // Notes on the sheet:
  //   IC1- P8-(X'Y')' 
  //   IC2-P3-(YZ')'
  //   IC2-PIN6-(XY')'
  //   IC2-PIN11-(YZ)'
  //   IC2-PIN8-(X'Y)'
  //   IC3-PIN11-(X'Z')'
  //   IC3-PIN3-(XZ)'
  //   IC3-PIN6-(Y'Z)'
  //   IC4-PIN12-(X'YZ')'
  //   IC5-PIN6-(X'Z)'
  //   IC6-PIN3-(Y'Z')'
  //   IC6-PIN6-(XZ')'
  //   IC6-PIN11-(XY)'
  //   IC4-PIN8-(X'Y'Z')'
  //   IC8-pin3-a0
  //   IC7-PIN6-C0
  //   IC7-PIN12
  //   IC7-PIN8
endmodule
