// Logisim project Decoder_Implementation.circ as structural Verilog: 1 circuit, main circuit main
module main (
  input  [2:0] xyz
);

  wire a0_out, a_out, b0_out, b_out, c0_out, c_out, d0_out, d_out, decoder_1_out0, decoder_1_out1,
       decoder_1_out2, decoder_1_out3, decoder_1_out4, decoder_1_out5, decoder_1_out6, e0_out, e_out, f0_out,
       f_out, g0_out, g_out, or_1_out, or_2_out, or_3_out, or_4_out, or_5_out, or_6_out, or_7_out, or_8_out,
       or_9_out, or_10_out, or_11_out, or_12_out, or_13_out, or_14_out;

  Decoder #(.select(3)) decoder_1 (
    .out0(decoder_1_out0), .out1(decoder_1_out1), .out2(decoder_1_out2), .out3(decoder_1_out3),
    .out4(decoder_1_out4), .out5(decoder_1_out5), .out6(decoder_1_out6), .sel(xyz));  // open: out7, en
  or or_1 (or_1_out, decoder_1_out1, decoder_1_out2, decoder_1_out3);
  or a (a_out, or_1_out, or_2_out);
  or or_2 (or_2_out, decoder_1_out4, decoder_1_out5, decoder_1_out6);
  or or_3 (or_3_out, decoder_1_out0, decoder_1_out1, decoder_1_out2);
  or b (b_out, or_3_out, decoder_1_out4, decoder_1_out6);
  or or_4 (or_4_out, decoder_1_out0, decoder_1_out1, decoder_1_out2);
  or c (c_out, or_4_out, decoder_1_out6);
  or or_5 (or_5_out, decoder_1_out2, decoder_1_out4, decoder_1_out5);
  or d (d_out, or_5_out, decoder_1_out6);
  or e (e_out, decoder_1_out3, decoder_1_out4, decoder_1_out5);
  or or_6 (or_6_out, decoder_1_out0, decoder_1_out2, decoder_1_out3);
  or f (f_out, or_6_out, decoder_1_out5);
  or or_7 (or_7_out, decoder_1_out0, decoder_1_out2, decoder_1_out3);
  or g (g_out, or_7_out, decoder_1_out4, decoder_1_out6);
  or or_8 (or_8_out, decoder_1_out0, decoder_1_out1, decoder_1_out2);
  or or_9 (or_9_out, decoder_1_out0, decoder_1_out1, decoder_1_out3);
  or or_10 (or_10_out, decoder_1_out0, decoder_1_out3, decoder_1_out5);
  or d0 (d0_out, or_10_out, decoder_1_out6);
  or or_11 (or_11_out, decoder_1_out0, decoder_1_out1, decoder_1_out2);
  or or_12 (or_12_out, decoder_1_out3, decoder_1_out4, decoder_1_out5);
  or or_13 (or_13_out, decoder_1_out1, decoder_1_out2, decoder_1_out3);
  or or_14 (or_14_out, decoder_1_out1, decoder_1_out2, decoder_1_out4);
  or a0 (a0_out, decoder_1_out2, decoder_1_out5);
  or b0 (b0_out, or_8_out, decoder_1_out3, decoder_1_out6);
  or c0 (c0_out, or_9_out, decoder_1_out4, decoder_1_out6);
  or e0 (e0_out, or_11_out, or_12_out, decoder_1_out6);
  or f0 (f0_out, or_13_out, decoder_1_out4, decoder_1_out5);
  or g0 (g0_out, or_14_out, decoder_1_out5, decoder_1_out6);
  _7_Segment_Display u_7_segment_display_1 (
    .g(g_out), .f(f_out), .a(a_out), .b(b_out), .e(e_out), .d(d_out), .c(c_out));  // open: dp
  _7_Segment_Display u_7_segment_display_2 (
    .g(g0_out), .f(f0_out), .a(a0_out), .b(b0_out), .e(e0_out), .d(d0_out), .c(c0_out));  // open: dp
endmodule
