// Logisim project Multiplexer_Implementations.circ as structural Verilog: 1 circuit, main circuit main
module main (
  input  [2:0] xyz,
  input  in_2,
  input  in_3,
  input  in_4,
  input  in_5,
  input  in_6,
  input  in_7,
  input  in_8,
  input  in_9,
  input  in_10,
  input  in_11,
  input  in_12,
  input  in_13,
  input  in_14,
  input  in_15,
  input  in_16,
  input  in_17,
  input  in_18,
  input  in_19,
  input  in_20,
  input  in_21,
  input  in_22,
  input  in_23,
  input  in_24,
  input  in_25,
  input  in_26,
  input  in_27,
  input  in_28,
  input  in_29,
  input  in_30,
  input  in_31,
  input  in_32,
  input  in_33,
  input  in_34,
  input  in_35,
  input  in_36,
  input  in_37,
  input  in_38,
  input  in_39,
  input  in_40,
  input  in_41,
  input  in_42,
  input  in_43,
  input  in_44,
  input  in_45,
  input  in_46,
  input  in_47,
  input  in_48,
  input  in_49,
  input  in_50,
  input  in_51,
  input  in_52,
  input  in_53,
  input  in_54,
  input  in_55,
  input  in_56,
  input  in_57,
  input  in_58,
  input  in_59,
  input  in_60,
  input  in_61,
  input  in_62,
  input  in_63,
  input  in_64,
  input  in_65,
  input  in_66,
  input  in_67,
  input  in_68,
  input  in_69,
  input  in_70,
  input  in_71,
  input  in_72,
  input  in_73,
  input  in_74,
  input  in_75,
  input  in_76,
  input  in_77,
  input  in_78,
  input  in_79,
  input  in_80,
  input  in_81,
  input  in_82,
  input  in_83,
  input  in_84,
  input  in_85,
  input  in_86,
  input  in_87,
  input  in_88,
  input  in_89,
  input  in_90,
  input  in_91,
  input  in_92,
  input  in_93,
  input  in_94,
  input  in_95,
  input  in_96,
  input  in_97,
  input  in_98,
  input  in_99,
  input  in_100,
  input  in_101,
  input  in_102,
  input  in_103,
  input  in_104,
  input  in_105,
  input  in_106,
  input  in_107,
  input  in_108,
  input  in_109,
  input  in_110,
  input  in_111,
  input  in_112,
  input  in_113
);

  wire multiplexer_1_out, multiplexer_2_out, multiplexer_3_out, multiplexer_4_out, multiplexer_5_out,
       multiplexer_6_out, multiplexer_7_out, multiplexer_8_out, multiplexer_9_out, multiplexer_10_out,
       multiplexer_11_out, multiplexer_12_out, multiplexer_13_out, multiplexer_14_out;

  Multiplexer #(.select(3)) multiplexer_1 (
    .in0(in_2), .in1(in_4), .in2(in_6), .in3(in_8), .in4(in_10), .in5(in_12), .in6(in_14), .in7(in_16),
    .out(multiplexer_1_out), .sel(xyz));  // open: en
  Multiplexer #(.select(3)) multiplexer_2 (
    .in0(in_18), .in1(in_20), .in2(in_22), .in3(in_24), .in4(in_26), .in5(in_28), .in6(in_30), .in7(in_32),
    .out(multiplexer_2_out), .sel(xyz));  // open: en
  Multiplexer #(.select(3)) multiplexer_3 (
    .in0(in_34), .in1(in_36), .in2(in_38), .in3(in_40), .in4(in_42), .in5(in_44), .in6(in_46), .in7(in_48),
    .out(multiplexer_3_out), .sel(xyz));  // open: en
  Multiplexer #(.select(3)) multiplexer_4 (
    .in0(in_50), .in1(in_52), .in2(in_54), .in3(in_56), .in4(in_58), .in5(in_60), .in6(in_62), .in7(in_64),
    .out(multiplexer_4_out), .sel(xyz));  // open: en
  Multiplexer #(.select(3)) multiplexer_5 (
    .in0(in_66), .in1(in_68), .in2(in_70), .in3(in_72), .in4(in_74), .in5(in_76), .in6(in_78), .in7(in_80),
    .out(multiplexer_5_out), .sel(xyz));  // open: en
  Multiplexer #(.select(3)) multiplexer_6 (
    .in0(in_82), .in1(in_84), .in2(in_86), .in3(in_88), .in4(in_90), .in5(in_92), .in6(in_94), .in7(in_96),
    .out(multiplexer_6_out), .sel(xyz));  // open: en
  Multiplexer #(.select(3)) multiplexer_7 (
    .in0(in_98), .in1(in_100), .in2(in_102), .in3(in_104), .in4(in_106), .in5(in_108), .in6(in_110),
    .in7(in_112), .out(multiplexer_7_out), .sel(xyz));  // open: en
  _7_Segment_Display u_7_segment_display_1 (
    .g(multiplexer_7_out), .f(multiplexer_6_out), .a(multiplexer_1_out), .b(multiplexer_2_out),
    .e(multiplexer_5_out), .d(multiplexer_4_out), .c(multiplexer_3_out));  // open: dp
  _7_Segment_Display u_7_segment_display_2 (
    .g(multiplexer_14_out), .f(multiplexer_13_out), .a(multiplexer_8_out), .b(multiplexer_9_out),
    .e(multiplexer_12_out), .d(multiplexer_11_out), .c(multiplexer_10_out));  // open: dp
  Multiplexer #(.select(3)) multiplexer_8 (
    .in0(in_3), .in1(in_5), .in2(in_7), .in3(in_9), .in4(in_11), .in5(in_13), .in6(in_15), .in7(in_17),
    .out(multiplexer_8_out), .sel(xyz));  // open: en
  Multiplexer #(.select(3)) multiplexer_9 (
    .in0(in_19), .in1(in_21), .in2(in_23), .in3(in_25), .in4(in_27), .in5(in_29), .in6(in_31), .in7(in_33),
    .out(multiplexer_9_out), .sel(xyz));  // open: en
  Multiplexer #(.select(3)) multiplexer_10 (
    .in0(in_35), .in1(in_37), .in2(in_39), .in3(in_41), .in4(in_43), .in5(in_45), .in6(in_47), .in7(in_49),
    .out(multiplexer_10_out), .sel(xyz));  // open: en
  Multiplexer #(.select(3)) multiplexer_11 (
    .in0(in_51), .in1(in_53), .in2(in_55), .in3(in_57), .in4(in_59), .in5(in_61), .in6(in_63), .in7(in_65),
    .out(multiplexer_11_out), .sel(xyz));  // open: en
  Multiplexer #(.select(3)) multiplexer_12 (
    .in0(in_67), .in1(in_69), .in2(in_71), .in3(in_73), .in4(in_75), .in5(in_77), .in6(in_79), .in7(in_81),
    .out(multiplexer_12_out), .sel(xyz));  // open: en
  Multiplexer #(.select(3)) multiplexer_13 (
    .in0(in_83), .in1(in_85), .in2(in_87), .in3(in_89), .in4(in_91), .in5(in_93), .in6(in_95), .in7(in_97),
    .out(multiplexer_13_out), .sel(xyz));  // open: en
  Multiplexer #(.select(3)) multiplexer_14 (
    .in0(in_99), .in1(in_101), .in2(in_103), .in3(in_105), .in4(in_107), .in5(in_109), .in6(in_111),
    .in7(in_113), .out(multiplexer_14_out), .sel(xyz));  // open: en
endmodule
