// Logisim project POS(Simplified)_NOR_Implementation.circ as structural Verilog: 1 circuit, main circuit main
module main (
  input  e,
  input  X,
  input  Y,
  input  Z
);

  wire a0_out, a_out, b0_out, b_out, c0_out, c_out, d0_out, d_out, e_out, f0_out, f_out, g0_out, g_out,
       nor_1_out, nor_2_out, nor_3_out, nor_4_out, nor_5_out, nor_6_out, nor_7_out, nor_8_out, nor_9_out,
       nor_10_out, nor_11_out, nor_12_out, nor_13_out, nor_14_out, not_1_out, not_2_out, not_3_out;

  not not_1 (not_1_out, X);
  not not_2 (not_2_out, Y);
  not not_3 (not_3_out, Z);
  nor nor_1 (nor_1_out, Y, Z);
  nor nor_2 (nor_2_out, X, not_2_out, Z);
  nor nor_3 (nor_3_out, not_1_out, Y, Z);
  nor nor_4 (nor_4_out, not_1_out, not_2_out);
  nor nor_5 (nor_5_out, X, Y, Z);
  nor nor_6 (nor_6_out, not_1_out, not_3_out);
  nor nor_7 (nor_7_out, not_2_out, not_3_out);
  nor nor_8 (nor_8_out, not_1_out, Y);
  nor nor_9 (nor_9_out, X, Y);
  nor nor_10 (nor_10_out, X, not_3_out);
  nor nor_11 (nor_11_out, not_2_out, Z);
  nor nor_12 (nor_12_out, X, Y, not_3_out);
  nor nor_13 (nor_13_out, not_1_out, Z);
  nor nor_14 (nor_14_out, Y, not_3_out);
  nor a (a_out, nor_5_out, nor_5_out);
  nor b (b_out, nor_6_out, nor_7_out);
  nor c (c_out, nor_7_out, nor_8_out);
  nor d (d_out, nor_9_out, nor_10_out);
  nor u_e (e_out, nor_9_out, nor_11_out);
  nor f (f_out, nor_12_out, nor_13_out);
  nor g (g_out, nor_14_out, nor_14_out);
  nor a0 (a0_out, nor_1_out, nor_10_out, nor_13_out);
  nor b0 (b0_out, nor_8_out, nor_8_out);
  nor c0 (c0_out, nor_2_out, nor_6_out);
  nor d0 (d0_out, nor_3_out, nor_12_out, nor_2_out);
  nor f0 (f0_out, nor_5_out, nor_4_out);
  nor g0 (g0_out, nor_5_out, nor_7_out);
  _7_Segment_Display u_7_segment_display_1 (
    .g(g_out), .f(f_out), .a(a_out), .b(b_out), .e(e_out), .d(d_out), .c(c_out));  // open: dp
  _7_Segment_Display u_7_segment_display_2 (
    .g(g0_out), .f(f0_out), .a(a0_out), .b(b0_out), .e(e), .d(d0_out), .c(c0_out));  // open: dp
endmodule
