// Logisim project POS_1st_Display.circ as structural Verilog: 1 circuit, main circuit main
module main (
  input  X,
  input  Y,
  input  Z
);

  wire a_out, and_1_out, b_out, c_out, d_out, e_out, f_out, g_out, not_1_out, not_2_out, not_3_out, or_1_out,
       or_2_out, or_3_out, or_4_out, or_5_out, or_6_out;

  not not_1 (not_1_out, X);
  not not_2 (not_2_out, Y);
  not not_3 (not_3_out, Z);
  or a (a_out, X, Y, Z);
  or or_1 (or_1_out, X, not_2_out, not_3_out);
  or or_2 (or_2_out, not_1_out, Y, not_3_out);
  or or_3 (or_3_out, not_1_out, Y, Z);
  or or_4 (or_4_out, X, Y, not_3_out);
  or or_5 (or_5_out, X, not_2_out, Z);
  or or_6 (or_6_out, not_1_out, not_2_out, Z);
  and b (b_out, or_1_out, or_2_out);
  and and_1 (and_1_out, or_5_out, or_6_out);
  and d (d_out, a_out, or_1_out, or_4_out);
  and c (c_out, b_out, or_3_out);
  and e (e_out, a_out, or_4_out, and_1_out);
  and f (f_out, or_6_out, or_3_out, or_4_out);
  and g (g_out, or_4_out, or_2_out);
  _7_Segment_Display u_7_segment_display_1 (
    .g(g_out), .f(f_out), .a(a_out), .b(b_out), .e(e_out), .d(d_out), .c(c_out));  // open: dp

  // Notes on the sheet:
  //   X'
  //   Y'
  //   Z'
  //   X+Y+Z
  //   X+Y'+Z'
  //   X'+Y+Z'
  //   X+Y+Z'
  //   X+Y'+Z
  //   X'+Y'+Z
  //   X'+Y+Z
  //   (X+Y'+Z')(X'+Y+Z')
  //   (X+Y'+Z)(X'+Y'+Z)
  //   (X+Y+Z)(X+Y+Z')(X+Y'+Z')
  //   (X+Y'+Z')(X'+Y+Z')(X'+Y+Z)
  //   (X+Y+Z)(X+Y+Z')(X+Y'+Z)(X'+Y'+Z)
  //   (X+Y+Z')(X'+Y+Z)(X'+Y'+Z)
  //   (X+Y+Z')(X'+Y+Z')
endmodule
