// Logisim project Pos_2nd_Display.circ as structural Verilog: 1 circuit, main circuit main
module main (
  input  X,
  input  Y,
  input  Z,
  input  e
);

  wire a0_out, and_1_out, b0_out, c0_out, d0_out, f0_out, g0_out, not_1_out, not_2_out, not_3_out, or_1_out,
       or_2_out, or_3_out, or_4_out, or_5_out, or_6_out, or_7_out;

  not not_1 (not_1_out, X);
  not not_2 (not_2_out, Y);
  not not_3 (not_3_out, Z);
  or or_1 (or_1_out, X, Y, Z);
  or or_2 (or_2_out, X, Y, not_3_out);
  or or_3 (or_3_out, X, not_2_out, not_3_out);
  or or_4 (or_4_out, not_1_out, Y, Z);
  or or_5 (or_5_out, not_1_out, not_2_out, Z);
  or or_6 (or_6_out, X, not_2_out, Z);
  or or_7 (or_7_out, not_1_out, Y, not_3_out);
  and b0 (b0_out, or_4_out, or_7_out);
  and f0 (f0_out, or_1_out, or_5_out);
  and g0 (g0_out, or_1_out, or_3_out);
  and and_1 (and_1_out, or_1_out, or_2_out, or_3_out);
  and d0 (d0_out, or_2_out, or_6_out, or_4_out);
  and c0 (c0_out, or_6_out, or_7_out);
  and a0 (a0_out, and_1_out, or_4_out, or_5_out);
  _7_Segment_Display u_7_segment_display_1 (
    .g(g0_out), .f(f0_out), .a(a0_out), .b(b0_out), .e(e), .d(d0_out), .c(c0_out));  // open: dp

  // Notes on the sheet:
  //   X'
  //   Y'
  //   Z'
  //   X+Y+Z
  //   X+Y+Z'
  //   X+Y'+Z'
  //   X'+Y+Z
  //   X'+Y'+Z
  //   X+Y'+Z
  //   X'+Y+Z'
  //   (X'+Y+Z)(X'+Y+Z')
  //   (X+Y+Z)(X'+Y'+Z)
  //   (X+Y+Z)(X+Y'+Z')
  //   (X+Y+Z)(X+Y+Z')(X+Y'+Z')
  //   (X+Y+Z')(X+Y'+Z)(X'+Y+Z)
  //   (X+Y'+Z)(X'+Y+Z)
  //   (X+Y+Z)(X+Y+Z')(X+Y'+Z')(X'+Y+Z)(X'+Y'+Z)
endmodule
