// Logisim project SOP(simplified)_NAND_Implemetation.circ as structural Verilog: 1 circuit, main circuit main
module main (
  input  x,
  input  y,
  input  z,
  input  e0
);

  wire a0_out, a_out, b_out, c0_out, c_out, d0_out, d_out, e_out, f0_out, f_out, g0_out, g_out, nand_1_out,
       nand_2_out, nand_3_out, nand_4_out, nand_5_out, nand_6_out, nand_7_out, nand_8_out, nand_9_out,
       nand_10_out, nand_11_out, nand_12_out, nand_13_out, nand_14_out, nand_15_out;

  nand nand_1 (nand_1_out, x, x);
  nand nand_2 (nand_2_out, z, z);
  nand nand_3 (nand_3_out, y, y);
  nand nand_4 (nand_4_out, nand_1_out, nand_3_out);
  nand nand_5 (nand_5_out, y, nand_2_out);
  nand nand_6 (nand_6_out, x, nand_3_out);
  nand nand_7 (nand_7_out, y, z);
  nand nand_8 (nand_8_out, nand_1_out, y);
  nand nand_9 (nand_9_out, nand_1_out, nand_2_out);
  nand nand_10 (nand_10_out, x, z);
  nand nand_11 (nand_11_out, nand_1_out, y, nand_2_out);
  nand nand_12 (nand_12_out, nand_1_out, z);
  nand nand_13 (nand_13_out, nand_3_out, nand_2_out);
  nand nand_14 (nand_14_out, x, nand_2_out);
  nand nand_15 (nand_15_out, x, y);
  nand a (a_out, nand_1_out, nand_3_out, nand_2_out);
  nand b (b_out, nand_4_out, z);
  nand c (c_out, nand_4_out, nand_5_out);
  nand d (d_out, nand_5_out, nand_1_out);
  nand e (e_out, nand_6_out, nand_7_out);
  nand f (f_out, nand_8_out, nand_9_out, nand_10_out);
  nand g (g_out, nand_3_out, z);
  _7_Segment_Display u_7_segment_display_1 (
    .g(g_out), .f(f_out), .a(a_out), .b(b_out), .e(e_out), .d(d_out), .c(c_out));  // open: dp
  nand a0 (a0_out, nand_11_out, nand_10_out);
  nand c0 (c0_out, nand_12_out, nand_13_out, nand_14_out);
  nand d0 (d0_out, a_out, nand_15_out, nand_10_out, nand_7_out);
  nand f0 (f0_out, nand_8_out, nand_6_out, nand_2_out);
  nand g0 (g0_out, g_out, nand_5_out, nand_1_out);
  _7_Segment_Display u_7_segment_display_2 (
    .g(g0_out), .f(f0_out), .a(a0_out), .b(nand_6_out), .e(e0), .d(d0_out), .c(c0_out));  // open: dp
endmodule
