// Logisim project SOP_2nd_Display.circ as structural Verilog: 1 circuit, main circuit main
module main (
  input  X,
  input  Y,
  input  Z
);

  wire a_out, b_out, c_out, d_out, e_out, f_out, g_out, not_1_out, not_2_out, not_3_out, or_1_out, or_2_out,
       or_3_out, or_4_out, or_5_out, or_6_out, or_7_out, X_prime_Y_prime_Z_out, X_prime_Y_prime_Z_prime_out,
       X_prime_YZ_out, X_prime_YZ_prime_out, XY_prime_Z_out, XY_prime_Z_prime_out, XYZ_prime_out;

  not not_1 (not_1_out, X);
  not not_2 (not_2_out, Y);
  not not_3 (not_3_out, Z);
  and X_prime_YZ_prime (X_prime_YZ_prime_out, not_1_out, Y, not_3_out);
  and XY_prime_Z (XY_prime_Z_out, X, not_2_out, Z);
  and X_prime_Y_prime_Z_prime (X_prime_Y_prime_Z_prime_out, not_1_out, not_2_out, not_3_out);
  and X_prime_Y_prime_Z (X_prime_Y_prime_Z_out, not_1_out, not_2_out, Z);
  and X_prime_YZ (X_prime_YZ_out, not_1_out, Y, Z);
  and XYZ_prime (XYZ_prime_out, X, Y, not_3_out);
  and XY_prime_Z_prime (XY_prime_Z_prime_out, X, not_2_out, not_3_out);
  or or_1 (or_1_out, X_prime_Y_prime_Z_prime_out, X_prime_YZ_prime_out, X_prime_Y_prime_Z_out);
  or or_2 (or_2_out, X_prime_Y_prime_Z_prime_out, X_prime_YZ_out, XY_prime_Z_out);
  or or_3 (or_3_out, X_prime_YZ_prime_out, XY_prime_Z_out, X_prime_Y_prime_Z_prime_out);
  or or_4 (or_4_out, X_prime_Y_prime_Z_out, X_prime_YZ_out, XYZ_prime_out);
  or or_5 (or_5_out, X_prime_Y_prime_Z_out, X_prime_YZ_prime_out, X_prime_YZ_out);
  or or_6 (or_6_out, X_prime_Y_prime_Z_out, X_prime_YZ_prime_out, XY_prime_Z_prime_out);
  or or_7 (or_7_out, XYZ_prime_out, X_prime_Y_prime_Z_prime_out, X_prime_Y_prime_Z_out);
  or a (a_out, X_prime_YZ_prime_out, XY_prime_Z_out);
  or b (b_out, or_1_out, XYZ_prime_out, X_prime_YZ_out);
  or c (c_out, or_7_out, X_prime_YZ_out, XY_prime_Z_prime_out);
  or d (d_out, or_2_out, XYZ_prime_out);
  or e (e_out, or_3_out, or_4_out, XY_prime_Z_prime_out);
  or f (f_out, or_5_out, XY_prime_Z_prime_out, XY_prime_Z_out);
  or g (g_out, or_6_out, XY_prime_Z_out, XYZ_prime_out);
  _7_Segment_Display u_7_segment_display_1 (
    .g(g_out), .f(f_out), .a(a_out), .b(b_out), .e(e_out), .d(d_out), .c(c_out));  // open: dp
endmodule
