// Logisim project SOP_Simplification_1st_Display.circ as structural Verilog: 1 circuit, main circuit main
module main (
  input  X,
  input  Y,
  input  Z,
  input  e0
);

  wire a0_out, a_out, b0_out, b_out, c0_out, c_out, d0_out, d_out, e_out, f0_out, f_out, g0_out, g_out,
       not_1_out, not_2_out, not_3_out, or_1_out, x_prime_y_out, x_prime_y_prime_out,
       x_prime_y_prime_z_prime_out, x_prime_yz_prime_out, x_prime_z_out, x_prime_z_prime_out, xy_out,
       xy_prime_out, xz_out, xz_prime_out, y_prime_z_out, y_prime_z_prime_out, yz_out, yz_prime_2_out,
       yz_prime_out;

  not not_1 (not_1_out, X);
  not not_2 (not_2_out, Y);
  not not_3 (not_3_out, Z);
  and x_prime_y_prime (x_prime_y_prime_out, not_1_out, not_2_out);
  and yz_prime (yz_prime_out, Y, not_3_out);
  and yz_prime_2 (yz_prime_2_out, Y, not_3_out);
  and xy_prime (xy_prime_out, X, not_2_out);
  and yz (yz_out, Y, Z);
  and x_prime_z_prime (x_prime_z_prime_out, not_1_out, not_3_out);
  and x_prime_y (x_prime_y_out, not_1_out, Y);
  and xz (xz_out, X, Z);
  and x_prime_z (x_prime_z_out, not_1_out, Z);
  and y_prime_z_prime (y_prime_z_prime_out, not_2_out, not_3_out);
  and xz_prime (xz_prime_out, X, not_3_out);
  and x_prime_y_prime_z_prime (x_prime_y_prime_z_prime_out, not_1_out, not_2_out, not_3_out);
  and xy (xy_out, X, Y);
  and y_prime_z (y_prime_z_out, not_2_out, Z);
  or a (a_out, X, Y, Z);
  or b (b_out, x_prime_y_prime_out, not_3_out);
  or c (c_out, x_prime_y_prime_out, yz_prime_out);
  or d (d_out, yz_prime_2_out, X);
  or e (e_out, xy_prime_out, yz_out);
  or f (f_out, x_prime_z_prime_out, x_prime_y_out, xz_out);
  or g (g_out, Y, not_3_out);
  and x_prime_yz_prime (x_prime_yz_prime_out, not_1_out, Y, not_3_out);
  or or_1 (or_1_out, xy_out, yz_out, xz_out);
  or a0 (a0_out, xz_out, x_prime_yz_prime_out);
  or b0 (b0_out, not_1_out, Y);
  or c0 (c0_out, x_prime_z_out, y_prime_z_prime_out, xz_prime_out);
  or d0 (d0_out, x_prime_y_prime_z_prime_out, or_1_out);
  or f0 (f0_out, Z, x_prime_y_out, xy_prime_out);
  or g0 (g0_out, X, yz_prime_out, y_prime_z_out);
  _7_Segment_Display u_7_segment_display_1 (
    .g(g_out), .f(f_out), .a(a_out), .b(b_out), .e(e_out), .d(d_out), .c(c_out));  // open: dp
  _7_Segment_Display u_7_segment_display_2 (
    .g(g0_out), .f(f0_out), .a(a0_out), .b(b0_out), .e(e0), .d(d0_out), .c(c0_out));  // open: dp
endmodule
